// Logisim project PTCY Disc - AIR - Ex 1.circ as structural Verilog: 1 circuit, main circuit main
module main (
  input  a,
  input  b,
  output Y,
  output out_4,
  output out_5
);

  wire and_1_out, and_2_out, and_3_out, and_4_out, and_5_out, and_6_out, and_7_out, not_1_out, not_2_out,
       not_3_out, not_4_out;

  not not_1 (not_1_out, a);
  not not_2 (not_2_out, b);
  not not_3 (not_3_out, out_4);
  not not_4 (not_4_out, out_4);
  and and_1 (and_1_out, not_1_out, b);
  and and_2 (and_2_out, out_4, b);
  and and_3 (and_3_out, a, out_4);
  and and_4 (and_4_out, out_5, a, not_2_out);
  and and_5 (and_5_out, not_3_out, a, b);
  and and_6 (and_6_out, not_4_out, out_5, a);
  and and_7 (and_7_out, out_5, a, not_2_out);
  or or_1 (out_4, and_1_out, and_2_out, and_3_out, and_4_out);
  or or_2 (out_5, and_5_out, and_6_out, and_7_out);
  and and_8 (Y, out_4, out_5);
endmodule
