// Logisim project PTCY Disc - AIR - Ex 2.circ as structural Verilog: 1 circuit, main circuit main
module main (
  input  [3:0] Xi,
  input  SYNC,
  output ACK,
  output [8:0] WYNIK
);

  wire adder_1_cout, adder_2_cout, clock_1_out, counter_1_carry, counter_2_carry, multiplexer_1_out,
       not_1_out, not_2_out, not_3_out, not_4_out, or_1_out, or_2_out;
  wire [2:0] counter_3_q;
  wire [6:0] adder_1_out, shift_register_1_q6;
  wire [8:0] adder_2_out;
  wire [15:0] rom_1_data;

  Shift_Register #(.length(7)) shift_register_1 (
    .shift(1'b0), .in(adder_1_cout), .clk(clock_1_out), .load(rom_1_data[8]), .clr(rom_1_data[10]),
    .d0(adder_1_out[6]), .q0(shift_register_1_q6[6]), .d1(adder_1_out[5]), .q1(shift_register_1_q6[5]),
    .d2(adder_1_out[4]), .q2(shift_register_1_q6[4]), .d3(adder_1_out[3]), .q3(shift_register_1_q6[3]),
    .d4(adder_1_out[2]), .q4(shift_register_1_q6[2]), .d5(adder_1_out[1]), .q5(shift_register_1_q6[1]),
    .d6(adder_1_out[0]), .q6(shift_register_1_q6[0]));  // open: out
  Shift_Register #(.length(9)) shift_register_2 (
    .shift(1'b0), .in(adder_2_cout), .clk(clock_1_out), .load(rom_1_data[7]), .clr(rom_1_data[10]),
    .d0(adder_2_out[8]), .q0(WYNIK[8]), .d1(adder_2_out[7]), .q1(WYNIK[7]), .d2(adder_2_out[6]),
    .q2(WYNIK[6]), .d3(adder_2_out[5]), .q3(WYNIK[5]), .d4(adder_2_out[4]), .q4(WYNIK[4]),
    .d5(adder_2_out[3]), .q5(WYNIK[3]), .d6(adder_2_out[2]), .q6(WYNIK[2]), .d7(adder_2_out[1]),
    .q7(WYNIK[1]), .d8(adder_2_out[0]), .q8(WYNIK[0]));  // open: out
  Adder #(.width(7)) adder_1 (
    .a({3'b000, Xi}), .b(shift_register_1_q6), .out(adder_1_out), .cin(1'b0), .cout(adder_1_cout));
  Adder #(.width(9)) adder_2 (
    .a({2'b00, shift_register_1_q6}), .b(WYNIK), .out(adder_2_out), .cin(1'b0), .cout(adder_2_cout));
  or or_1 (or_1_out, rom_1_data[9], rom_1_data[6]);
  Counter #(.width(3), .max('h7)) counter_1 (
    .load(or_1_out), .D(3'b100), .count(rom_1_data[6]), .carry(counter_1_carry), .clk(clock_1_out));  // open: Q, clr
  Counter #(.width(3), .max('h7)) counter_2 (
    .load(or_2_out), .D(3'b110), .count(rom_1_data[5]), .carry(counter_2_carry), .clk(clock_1_out));  // open: Q, clr
  or or_2 (or_2_out, rom_1_data[9], rom_1_data[5]);
  Clock clock_1 (.out(clock_1_out));
  not not_1 (not_1_out, counter_1_carry);
  not not_2 (not_2_out, SYNC);
  Multiplexer #(.select(3), .enable("false")) multiplexer_1 (
    .in0(SYNC), .in1(not_2_out), .in2(not_1_out), .in3(counter_2_carry), .in4(1'b1), .in5(1'b0), .in6(1'b0),
    .in7(1'b0), .out(multiplexer_1_out), .sel(rom_1_data[13:11]));
  not not_3 (not_3_out, multiplexer_1_out);
  Counter #(.width(3), .max('h7)) counter_3 (
    .load(not_3_out), .D(rom_1_data[2:0]), .count(multiplexer_1_out), .Q(counter_3_q), .clk(not_4_out));  // open: carry, clr
  not not_4 (not_4_out, clock_1_out);
  S_R_Flip_Flop s_r_ff_1 (.Q(ACK), .preset(rom_1_data[3]), .reset(rom_1_data[4]));  // open: S, clk, R, Qn, en
  ROM #(.addrWidth(3), .dataWidth(16)) rom_1 (.addr(counter_3_q), .data(rom_1_data));  // open: sel

  // Notes on the sheet:
  //   contents of rom_1 (hex, n*v repeats v):
  //   2608 11 1155 80b 2809 18b5 80e 2808
endmodule
