// Logisim project PTCY Disc - AIR - Ex 3.circ as structural Verilog: 1 circuit, main circuit main
module main (
  input  x,
  output Y,
  output out_3,
  output out_4
);

  wire and_1_out, and_2_out, clock_1_out, j_k_ff_2_qn, not_1_out, or_1_out;

  not not_1 (not_1_out, x);
  Clock clock_1 (.out(clock_1_out));
  and and_1 (and_1_out, out_3, j_k_ff_2_qn);
  and and_2 (and_2_out, out_3, not_1_out);
  or or_1 (or_1_out, x, and_1_out);
  J_K_Flip_Flop j_k_ff_1 (.J(out_4), .clk(clock_1_out), .K(or_1_out), .Q(out_3));  // open: Qn, preset, en, reset
  J_K_Flip_Flop j_k_ff_2 (
    .J(x), .clk(clock_1_out), .K(and_2_out), .Q(out_4), .Qn(j_k_ff_2_qn));  // open: preset, en, reset
  and and_3 (Y, out_3, j_k_ff_2_qn);
endmodule
