// Logisim project PTCY Disc - AIR - Ex 4.circ as structural Verilog: 1 circuit, main circuit main
module main (
  input  a,
  input  b,
  output out_3,
  output out_4,
  output out_5,
  output Y
);

  wire and_1_out, and_2_out, and_3_out, and_4_out, and_5_out, and_6_out, and_7_out, and_8_out, and_9_out,
       and_10_out, and_11_out, and_12_out, and_13_out, and_14_out, not_1_out, not_2_out, not_3_out,
       not_4_out, not_5_out, not_6_out;

  not not_1 (not_1_out, b);
  not not_2 (not_2_out, a);
  not not_3 (not_3_out, out_3);
  not not_4 (not_4_out, out_5);
  not not_5 (not_5_out, out_4);
  and and_1 (and_1_out, out_4, out_5, not_2_out, not_1_out);
  and and_2 (and_2_out, out_3, out_5, not_1_out);
  and and_3 (and_3_out, out_3, not_2_out);
  and and_4 (and_4_out, not_2_out, b);
  and and_5 (and_5_out, not_3_out, out_4, out_5, not_2_out);
  and and_6 (and_6_out, out_4, a, b);
  and and_7 (and_7_out, out_4, not_4_out, a);
  and and_8 (and_8_out, not_5_out, not_2_out, not_1_out);
  and and_9 (and_9_out, out_5, not_2_out, b);
  and and_10 (and_10_out, not_3_out, out_4, out_5);
  and and_11 (and_11_out, not_3_out, out_5, a, not_1_out);
  and and_12 (and_12_out, out_4, a, b);
  and and_13 (and_13_out, out_3, not_2_out);
  or or_1 (out_3, and_1_out, and_2_out, and_3_out);
  or or_2 (out_4, and_4_out, and_5_out, out_3, and_6_out, and_7_out);
  or or_3 (out_5, and_8_out, and_9_out, and_10_out, and_11_out, and_12_out, and_13_out);
  not not_6 (not_6_out, out_5);
  and and_14 (and_14_out, out_4, not_6_out);
  or or_4 (Y, out_3, and_14_out);
endmodule
