// Logisim project PTCY Disc - AIR - Ex 5.circ as structural Verilog: 1 circuit, main circuit main
module main (
  input  SYNC,
  input  [3:0] X,
  output ACK
);

  wire clock_1_out, multiplexer_2_out, not_2_out, not_3_out, not_4_out;
  wire [1:0] rom_1_data_3;
  wire [2:0] counter_1_q, multiplexer_1_out, not_1_out, rom_1_data;
  wire [3:0] adder_1_out, shift_register_1_q3;
  wire [5:4] rom_1_data_2;

  Shift_Register #(.length(4)) shift_register_1 (
    .shift(1'b0), .clk(clock_1_out), .load(rom_1_data_2[4]), .clr(rom_1_data_2[5]), .d0(adder_1_out[3]),
    .q0(shift_register_1_q3[3]), .d1(adder_1_out[2]), .q1(shift_register_1_q3[2]), .d2(adder_1_out[1]),
    .q2(shift_register_1_q3[1]), .d3(adder_1_out[0]), .q3(shift_register_1_q3[0]));  // open: in, out
  Multiplexer #(.width(3), .enable("false")) multiplexer_1 (
    .in0(X[2:0]), .in1(not_1_out), .out(multiplexer_1_out), .sel(X[3]));
  assign not_1_out = ~X[2:0];  // NOT_Gate not_1, 3 bits wide
  Clock clock_1 (.out(clock_1_out));
  Adder #(.width(4)) adder_1 (
    .a({X[3], multiplexer_1_out}), .b(shift_register_1_q3), .out(adder_1_out), .cin(X[3]));  // open: cout
  not not_2 (not_2_out, SYNC);
  Multiplexer #(.select(2), .enable("false")) multiplexer_2 (
    .in0(SYNC), .in1(not_2_out), .in2(1'b1), .in3(1'b0), .out(multiplexer_2_out), .sel(rom_1_data_3));
  not not_3 (not_3_out, clock_1_out);
  not not_4 (not_4_out, multiplexer_2_out);
  Counter #(.width(3), .max('h7)) counter_1 (
    .load(not_4_out), .D(rom_1_data), .count(multiplexer_2_out), .Q(counter_1_q), .clk(not_3_out));  // open: carry, clr
  ROM #(.addrWidth(3)) rom_1 (.addr(counter_1_q), .data({rom_1_data_3, rom_1_data_2, ACK, rom_1_data}));  // open: sel

  // Notes on the sheet:
  //   contents of rom_1 (hex, n*v repeats v):
  //   a8 1 92 4b 4 95 4e c8
endmodule
