// Logisim project PTCY Lecture - Chapter 4 - Mealy Automat Example.circ as structural Verilog: 1 circuit, main circuit main
module main (
  input  x1,
  input  x0,
  output out_3,
  output out_4,
  output out_5,
  output out_6
);

  wire and_1_out, and_2_out, and_3_out, and_4_out, and_5_out, and_6_out, and_7_out, and_8_out, and_9_out,
       and_10_out, and_11_out, and_12_out, and_13_out, and_14_out, and_15_out, and_16_out, clock_1_out,
       d_ff_1_qn, d_ff_2_qn, not_1_out, not_2_out, or_1_out, or_2_out, or_3_out;

  not not_1 (not_1_out, x1);
  Clock clock_1 (.out(clock_1_out));
  not not_2 (not_2_out, x0);
  and and_1 (and_1_out, d_ff_2_qn, x0);
  and and_2 (and_2_out, out_5, not_1_out, x0);
  and and_3 (and_3_out, d_ff_1_qn, out_6, not_1_out, not_2_out);
  and and_4 (and_4_out, x1, not_2_out);
  and and_5 (and_5_out, x1, out_6);
  and and_6 (and_6_out, d_ff_1_qn, d_ff_2_qn, not_1_out, x0);
  and and_7 (and_7_out, d_ff_1_qn, out_6, not_1_out, not_2_out);
  and and_8 (and_8_out, out_5, x1);
  D_Flip_Flop d_ff_1 (.clk(clock_1_out), .D(or_1_out), .Q(out_5), .Qn(d_ff_1_qn));  // open: preset, en, reset
  or or_1 (or_1_out, and_1_out, and_2_out, and_3_out);
  D_Flip_Flop d_ff_2 (.clk(clock_1_out), .D(or_2_out), .Q(out_6), .Qn(d_ff_2_qn));  // open: preset, en, reset
  or or_2 (or_2_out, and_4_out, and_5_out, and_6_out, and_7_out, and_8_out);
  or or_3 (or_3_out, not_1_out, not_2_out);
  and and_9 (and_9_out, d_ff_1_qn, out_6, not_1_out);
  and and_10 (and_10_out, out_6, not_1_out, x0);
  and and_11 (and_11_out, out_5, out_6, x1);
  and and_12 (and_12_out, out_5, x1, x0);
  and and_13 (and_13_out, out_5, d_ff_2_qn, not_1_out, not_2_out);
  and and_14 (and_14_out, d_ff_1_qn, not_1_out, not_2_out);
  and and_15 (and_15_out, d_ff_1_qn, out_6, or_3_out);
  and and_16 (and_16_out, d_ff_2_qn, x1, x0);
  or or_4 (out_3, and_9_out, and_10_out, and_11_out, and_12_out, and_13_out);
  or or_5 (out_4, and_14_out, and_15_out, and_16_out);
endmodule
