// Logisim project PTCY Script - Chapter 1 - Ex 15.circ as structural Verilog: 2 circuits, main circuit APN
module APN (
  input  x4,
  input  x3,
  input  x2,
  input  x1,
  input  x0,
  output Y
);

  wire nand_1_out, nand_2_out, nand_3_out, nand_4_out, nand_5_out, not_1_out, not_2_out, not_3_out,
       not_4_out, not_5_out;

  not not_1 (not_1_out, x4);
  not not_2 (not_2_out, x3);
  not not_3 (not_3_out, x1);
  not not_4 (not_4_out, x2);
  not not_5 (not_5_out, x0);
  nand nand_1 (nand_1_out, not_1_out, not_5_out);
  nand nand_2 (nand_2_out, x4, not_4_out, x1);
  nand nand_3 (nand_3_out, x4, not_2_out, x1);
  nand nand_4 (nand_4_out, x4, not_2_out, x0);
  nand nand_5 (nand_5_out, x4, x2, not_3_out);
  nand nand_6 (Y, nand_1_out, nand_2_out, nand_3_out, nand_4_out, nand_5_out);
endmodule

module KPN (
  input  x4,
  input  x3,
  input  x2,
  input  x1,
  input  x0,
  output Y
);

  wire nor_1_out, nor_2_out, nor_3_out, nor_4_out, not_1_out, not_2_out, not_3_out, not_4_out, not_5_out;

  not not_1 (not_1_out, x4);
  not not_2 (not_2_out, x3);
  not not_3 (not_3_out, x1);
  not not_4 (not_4_out, x2);
  not not_5 (not_5_out, x0);
  nor nor_1 (nor_1_out, x4, not_5_out);
  nor nor_2 (nor_2_out, not_1_out, x2, x1, x0);
  nor nor_3 (nor_3_out, not_1_out, not_2_out, x2, x1);
  nor nor_4 (nor_4_out, not_1_out, not_2_out, not_4_out, not_3_out);
  nor nor_5 (Y, nor_1_out, nor_2_out, nor_3_out, nor_4_out);
endmodule
