// Logisim project PTCY Script - Chapter 2 - Ex C8.circ as structural Verilog: 1 circuit, main circuit main
module main (
  input  x3,
  input  x2,
  input  x1,
  input  x0,
  output Y
);

  wire not_1_out, or_1_out;

  not not_1 (not_1_out, x0);
  or or_1 (or_1_out, x2, not_1_out);
  Multiplexer #(.select(2), .enable("false")) multiplexer_1 (
    .in0(or_1_out), .in1(not_1_out), .in2(x0), .in3(1'b0), .out(Y), .sel({x3, x1}));
endmodule
