// Logisim project PTCY Script - Chapter 3 - Ex A1.circ as structural Verilog: 1 circuit, main circuit main
module main (
  output out_1,
  output out_2,
  output out_3
);

  wire _1_qn, _3_qn, and_1_out, and_2_out, and_3_out, clock_1_out, xor_1_out;

  and and_1 (and_1_out, out_2, out_3);
  Clock clock_1 (.out(clock_1_out));
  D_Flip_Flop _3 (.clk(clock_1_out), .D(and_1_out), .Q(out_1), .Qn(_3_qn));  // open: preset, en, reset
  xor xor_1 (xor_1_out, out_2, out_3);
  and and_2 (and_2_out, xor_1_out, _3_qn);
  D_Flip_Flop _2 (.clk(clock_1_out), .D(and_2_out), .Q(out_2));  // open: Qn, preset, en, reset
  and and_3 (and_3_out, _1_qn, _3_qn);
  D_Flip_Flop _1 (.clk(clock_1_out), .D(and_3_out), .Q(out_3), .Qn(_1_qn));  // open: preset, en, reset
endmodule
