// Logisim project PTCY Script - Chapter 3 - Ex A7.circ as structural Verilog: 1 circuit, main circuit main
module main (
  output Y,
  output out_2,
  output out_3,
  output out_4
);

  wire and_1_out, and_2_out, and_3_out, and_4_out, clock_1_out, D0_qn, D2_qn, or_1_out, or_2_out, xnor_1_out;

  Clock clock_1 (.out(clock_1_out));
  and and_1 (and_1_out, out_2, D0_qn);
  and and_2 (and_2_out, D2_qn, out_3, out_4);
  and and_3 (and_3_out, out_3, D0_qn);
  and and_4 (and_4_out, D2_qn, out_4);
  or or_1 (or_1_out, and_1_out, and_2_out);
  or or_2 (or_2_out, and_3_out, and_4_out);
  D_Flip_Flop D2 (.clk(clock_1_out), .D(or_1_out), .Q(out_2), .Qn(D2_qn));  // open: preset, en, reset
  D_Flip_Flop D1 (.clk(clock_1_out), .D(or_2_out), .Q(out_3));  // open: Qn, preset, en, reset
  D_Flip_Flop D0 (.clk(clock_1_out), .D(D0_qn), .Q(out_4), .Qn(D0_qn));  // open: preset, en, reset
  xnor xnor_1 (xnor_1_out, out_2, out_3);
  and and_5 (Y, xnor_1_out, out_4);
endmodule
