// Logisim project PTCY Script - Chapter 3 - Ex A8.circ as structural Verilog: 1 circuit, main circuit main
module main (
  output out_1,
  output out_2,
  output out_3
);

  wire and_1_out, and_2_out, and_3_out, clock_1_out, D0_qn, D1_qn, D2_qn, or_1_out, xnor_1_out;

  Clock clock_1 (.out(clock_1_out));
  xnor xnor_1 (xnor_1_out, out_2, out_3);
  and and_1 (and_1_out, D2_qn, out_3);
  and and_2 (and_2_out, D2_qn, out_2);
  and and_3 (and_3_out, out_1, D1_qn, D0_qn);
  or or_1 (or_1_out, and_1_out, and_2_out, and_3_out);
  D_Flip_Flop D2 (.clk(clock_1_out), .D(or_1_out), .Q(out_1), .Qn(D2_qn));  // open: preset, en, reset
  D_Flip_Flop D1 (.clk(clock_1_out), .D(xnor_1_out), .Q(out_2), .Qn(D1_qn));  // open: preset, en, reset
  D_Flip_Flop D0 (.clk(clock_1_out), .D(D0_qn), .Q(out_3), .Qn(D0_qn));  // open: preset, en, reset
endmodule
