// Logisim project PTCY Script - Chapter 3 - Ex B8.circ as structural Verilog: 2 circuits, main circuit D Flip Flops
module D_Flip_Flops (
  input  x,
  output Y
);

  wire clock_1_out, nand_1_out, nand_2_out, nand_3_out, nand_4_out, nand_5_out, nand_6_out, not_1_out,
       not_2_out, Q0_q, Q0_qn, Q1_q, Q2_q, Q2_qn;

  Clock clock_1 (.out(clock_1_out));
  not not_1 (not_1_out, x);
  nand nand_1 (nand_1_out, Q2_q, x);
  nand nand_2 (nand_2_out, Q1_q, Q0_q, x);
  nand nand_3 (nand_3_out, Q2_qn, Q0_qn, not_1_out);
  not not_2 (not_2_out, nand_4_out);
  nand nand_4 (nand_4_out, Q2_qn, Q1_q);
  nand nand_5 (nand_5_out, nand_1_out, nand_2_out, nand_3_out);
  D_Flip_Flop Q2 (.clk(clock_1_out), .D(not_2_out), .Q(Q2_q), .Qn(Q2_qn));  // open: preset, en, reset
  D_Flip_Flop Q1 (.clk(clock_1_out), .D(Q2_qn), .Q(Q1_q));  // open: Qn, preset, en, reset
  D_Flip_Flop Q0 (.clk(clock_1_out), .D(nand_5_out), .Q(Q0_q), .Qn(Q0_qn));  // open: preset, en, reset
  nand nand_6 (nand_6_out, Q2_q, Q0_q);
  not not_3 (Y, nand_6_out);
endmodule

module JK_Flip_Flops (
  input  x,
  output Y
);

  wire clock_1_out, nand_1_out, nand_2_out, nand_3_out, nand_4_out, nand_5_out, nand_6_out, not_1_out,
       not_2_out, Q0_q, Q1_q, Q1_qn, Q2_q, Q2_qn;

  Clock clock_1 (.out(clock_1_out));
  not not_1 (not_1_out, x);
  nand nand_1 (nand_1_out, Q2_qn, not_1_out);
  nand nand_2 (nand_2_out, Q2_q, x);
  not not_2 (not_2_out, not_1_out);
  nand nand_3 (nand_3_out, Q1_qn, x);
  J_K_Flip_Flop Q2 (.J(Q1_q), .clk(clock_1_out), .K(1'b1), .Q(Q2_q), .Qn(Q2_qn));  // open: preset, en, reset
  J_K_Flip_Flop Q1 (.J(1'b1), .clk(clock_1_out), .K(Q2_q), .Q(Q1_q), .Qn(Q1_qn));  // open: preset, en, reset
  nand nand_4 (nand_4_out, nand_1_out, nand_2_out);
  J_K_Flip_Flop Q0 (.J(nand_4_out), .clk(clock_1_out), .K(nand_5_out), .Q(Q0_q));  // open: Qn, preset, en, reset
  nand nand_5 (nand_5_out, not_2_out, nand_3_out);
  nand nand_6 (nand_6_out, Q2_q, Q0_q);
  not not_3 (Y, nand_6_out);
endmodule
