// Logisim project PTCY Script - Chapter 3 - Ex C3.circ as structural Verilog: 1 circuit, main circuit main
module main (
  input  x1,
  input  x0,
  output out_3,
  output out_4
);

  wire clock_1_out, multiplexer_1_out, multiplexer_2_out, not_1_out;

  Clock clock_1 (.out(clock_1_out));
  not not_1 (not_1_out, x0);
  Multiplexer #(.select(3), .enable("false")) multiplexer_1 (
    .in0(not_1_out), .in1(1'b1), .in2(1'b1), .in3(x0), .in4(1'b1), .in5(x0), .in6(not_1_out), .in7(1'b1),
    .out(multiplexer_1_out), .sel({out_3, out_4, x1}));
  Multiplexer #(.select(3), .enable("false")) multiplexer_2 (
    .in0(1'b1), .in1(1'b1), .in2(1'b1), .in3(1'b0), .in4(1'b1), .in5(1'b0), .in6(1'b0), .in7(1'b0),
    .out(multiplexer_2_out), .sel({out_4, x1, x0}));
  D_Flip_Flop D1 (.clk(clock_1_out), .D(multiplexer_1_out), .Q(out_3));  // open: Qn, preset, en, reset
  D_Flip_Flop D0 (.clk(clock_1_out), .D(multiplexer_2_out), .Q(out_4));  // open: Qn, preset, en, reset
endmodule
