// Logisim project PTCY Script - Chapter 3 - Ex C4.circ as structural Verilog: 1 circuit, main circuit main
module main (
  input  X1,
  input  X0,
  output out_3,
  output out_4
);

  wire clock_1_out, multiplexer_1_out, multiplexer_2_out;

  Clock clock_1 (.out(clock_1_out));
  Multiplexer #(.select(3), .enable("false")) multiplexer_1 (
    .in0(1'b0), .in1(1'b1), .in2(X0), .in3(X0), .in4(X0), .in5(X0), .in6(1'b0), .in7(1'b1),
    .out(multiplexer_1_out), .sel({out_3, out_4, X1}));
  Multiplexer #(.select(3), .enable("false")) multiplexer_2 (
    .in0(1'b0), .in1(1'b1), .in2(1'b1), .in3(1'b1), .in4(1'b0), .in5(1'b0), .in6(1'b0), .in7(1'b1),
    .out(multiplexer_2_out), .sel({out_4, X1, X0}));
  D_Flip_Flop D1 (.clk(clock_1_out), .D(multiplexer_1_out), .Q(out_3));  // open: Qn, preset, en, reset
  D_Flip_Flop D0 (.clk(clock_1_out), .D(multiplexer_2_out), .Q(out_4));  // open: Qn, preset, en, reset
endmodule
