// Logisim project PTCY Script - Chapter 5 - Ex 2.circ as structural Verilog: 1 circuit, main circuit main
module main (
  input  G,
  input  F,
  output Y,
  output out_4,
  output out_5
);

  wire and_1_out, and_2_out, and_3_out, and_4_out, and_5_out, not_1_out, not_2_out;

  not not_1 (not_1_out, G);
  not not_2 (not_2_out, out_4);
  and and_1 (and_1_out, out_5, G);
  and and_2 (and_2_out, out_4, F);
  and and_3 (and_3_out, not_2_out, out_5);
  and and_4 (and_4_out, out_5, G);
  and and_5 (and_5_out, not_2_out, not_1_out, F);
  or q1_prime (out_4, and_1_out, and_2_out);
  or q0_prime (out_5, and_3_out, and_4_out, and_5_out);
  and u_Y (Y, out_4, out_5);

  // Notes on the sheet:
  //   By uruchomić automat przeklikaj następującą sekwencję do ostatniego elementu: (0,1)(1,1)(1,0)(0,0).
endmodule
