// Logisim project PTCY Script - Chapter 5 - Ex 6.circ as structural Verilog: 1 circuit, main circuit main
module main (
  input  C,
  input  D,
  output y,
  output out_4,
  output out_5
);

  wire and_1_out, and_2_out, and_3_out, and_4_out, and_5_out, and_6_out, not_1_out;

  not not_1 (not_1_out, C);
  and and_1 (and_1_out, not_1_out, D);
  and and_2 (and_2_out, out_4, C);
  and and_3 (and_3_out, out_5, D);
  and and_4 (and_4_out, out_5, not_1_out);
  and and_5 (and_5_out, out_4, out_5);
  and and_6 (and_6_out, out_4, C);
  or q1_prime (out_4, and_1_out, and_2_out, and_3_out);
  or q0_prime (out_5, and_4_out, and_5_out, and_6_out);

  assign y = out_5;

  // Notes on the sheet:
  //   By uruchomić automat przeklikaj sekwencję do ostatniego elementu: (0,1)(1,1)(1,0)(0,0)(1,0)(0,0).
endmodule
