// Logisim project PTCY Script - Chapter 5 - Ex 7.circ as structural Verilog: 1 circuit, main circuit main
module main (
  input  C,
  input  T,
  output Y,
  output out_4,
  output out_5
);

  wire _1_out, _2_out, _3_out, _4_out, _5_out, _6_out, _7_out, _8_out, not_1_out, not_2_out, not_3_out;

  not not_1 (not_1_out, C);
  not not_2 (not_2_out, T);
  and _1 (_1_out, out_5, not_2_out);
  and _2 (_2_out, out_4, C);
  and _3 (_3_out, not_3_out, not_1_out, T);
  and _4 (_4_out, out_4, not_3_out, T);
  and _5 (_5_out, out_5, not_1_out);
  and _6 (_6_out, out_4, C);
  and _7 (_7_out, out_5, not_2_out);
  and _8 (_8_out, out_4, out_5, T);
  or q1_prime (out_4, _1_out, _2_out, _3_out, _4_out);
  or q0_prime (out_5, _5_out, _6_out, _7_out, _8_out);
  not not_3 (not_3_out, out_5);

  assign Y = out_5;

  // Notes on the sheet:
  //   By uruchomić automat odłącz i przyłącz ponownie wejście pierwsze od góry w bramce nr 7, a następnie przeklikaj sekwencję do ostatniego elementu: (0,0)(0,1)(1,1)(1,0).
endmodule
