// Logisim project PTCY Script - Chapter 5 - Ex 8.circ as structural Verilog: 1 circuit, main circuit main
module main (
  input  C,
  input  T,
  output Y,
  output out_4,
  output out_5
);

  wire _1_out, _2_out, _3_out, _4_out, _5_out, _6_out, _7_out, not_1_out, not_2_out, not_3_out, not_4_out;

  not not_1 (not_1_out, C);
  not not_2 (not_2_out, T);
  not not_3 (not_3_out, out_5);
  not not_4 (not_4_out, out_5);
  and _1 (_1_out, out_5, not_2_out);
  and _2 (_2_out, out_4, not_1_out);
  and _3 (_3_out, not_3_out, C, T);
  and _4 (_4_out, out_4, not_4_out, T);
  and _5 (_5_out, out_4, not_1_out);
  and _6 (_6_out, out_5, C);
  and _7 (_7_out, out_4, out_5);
  or q1_prime (out_4, _1_out, _2_out, _3_out, _4_out);
  or q0_prime (out_5, _5_out, _6_out, _7_out);

  assign Y = out_5;

  // Notes on the sheet:
  //   By uruchomić automat odłączyć i przyłączyć ponownie pierwsze wejście od góry przy bramce nr 1, a następnie przeklikać sekwencję do ostatniego elementu(0,0)(1,0)(1,1)(0,1)(0,0).
endmodule
