// Logisim project PTCY Script - Chapter 6 - Ex 1.circ as structural Verilog: 1 circuit, main circuit main
module main (
  input  [3:0] WE1,
  input  [3:0] WE2,
  input  SYNC,
  output ACK,
  output WYN,
  output [4:0] out_6
);

  wire adder_1_cout, CK_out, d_ff_1_qn, d_ff_2_qn, d_ff_3_qn, multiplexer_1_out, not_1_out, not_2_out,
       not_3_out, not_4_out, not_5_out, not_6_out, not_7_out, not_8_out;
  wire [1:0] rom_1_data_3;
  wire [3:0] adder_1_out, counter_1_q, rom_1_data, shift_register_1_q3, shift_register_2_q3;
  wire [15:4] rom_1_data_2;

  Shift_Register #(.length(4)) shift_register_1 (
    .shift(1'b0), .clk(CK_out), .load(rom_1_data_2[7]), .clr(d_ff_1_qn), .d0(WE1[3]),
    .q0(shift_register_1_q3[3]), .d1(WE1[2]), .q1(shift_register_1_q3[2]), .d2(WE1[1]),
    .q2(shift_register_1_q3[1]), .d3(WE1[0]), .q3(shift_register_1_q3[0]));  // open: in, out
  not not_1 (not_1_out, rom_1_data_2[10]);
  D_Flip_Flop d_ff_1 (.clk(CK_out), .D(not_1_out), .Qn(d_ff_1_qn));  // open: Q, preset, en, reset
  Shift_Register #(.length(4)) shift_register_2 (
    .shift(1'b0), .clk(CK_out), .load(rom_1_data_2[6]), .clr(d_ff_2_qn), .d0(WE2[3]),
    .q0(shift_register_2_q3[3]), .d1(WE2[2]), .q1(shift_register_2_q3[2]), .d2(WE2[1]),
    .q2(shift_register_2_q3[1]), .d3(WE2[0]), .q3(shift_register_2_q3[0]));  // open: in, out
  D_Flip_Flop d_ff_2 (.clk(CK_out), .D(not_2_out), .Qn(d_ff_2_qn));  // open: Q, preset, en, reset
  not not_2 (not_2_out, rom_1_data_2[9]);
  Adder #(.width(4)) adder_1 (
    .a(shift_register_2_q3), .b(shift_register_1_q3), .out(adder_1_out), .cout(adder_1_cout));  // open: cin
  Shift_Register #(.length(5)) shift_register_3 (
    .shift(1'b0), .clk(CK_out), .load(rom_1_data_2[8]), .clr(d_ff_3_qn), .d0(adder_1_cout), .q0(out_6[4]),
    .d1(adder_1_out[3]), .q1(out_6[3]), .d2(adder_1_out[2]), .q2(out_6[2]), .d3(adder_1_out[1]),
    .q3(out_6[1]), .d4(adder_1_out[0]), .q4(out_6[0]));  // open: in, out
  not not_3 (not_3_out, rom_1_data_2[11]);
  Clock CK (.out(CK_out));
  D_Flip_Flop d_ff_3 (.clk(CK_out), .D(not_3_out), .Qn(d_ff_3_qn));  // open: Q, preset, en, reset
  not not_4 (not_4_out, SYNC);
  Multiplexer #(.select(2), .enable("false")) multiplexer_1 (
    .in0(SYNC), .in1(not_4_out), .in2(1'b1), .in3(1'b0), .out(multiplexer_1_out), .sel(rom_1_data_3));
  not not_5 (not_5_out, multiplexer_1_out);
  not not_6 (not_6_out, CK_out);
  // Probe on rom_1_data_2[14]
  // Probe on rom_1_data_2[15]
  Counter #(.width(4), .max('hf)) counter_1 (
    .load(not_5_out), .D(rom_1_data), .count(multiplexer_1_out), .Q(counter_1_q), .clk(not_6_out));  // open: carry, clr
  ROM #(.addrWidth(4), .dataWidth(16)) rom_1 (
    .addr(counter_1_q), .data({rom_1_data_2[15:14], rom_1_data_3, rom_1_data_2[11:4], rom_1_data}));  // open: sel
  not not_7 (not_7_out, rom_1_data_2[5]);
  not not_8 (not_8_out, rom_1_data_2[4]);
  D_Flip_Flop d_ff_4 (.clk(CK_out), .D(not_7_out), .Qn(ACK));  // open: Q, preset, en, reset
  D_Flip_Flop d_ff_5 (.clk(CK_out), .D(not_8_out), .Qn(WYN));  // open: Q, preset, en, reset

  // Notes on the sheet:
  //   n = 4
  //   contents of rom_1 (hex, n*v repeats v):
  //   2e20 1 2080 1023 4 2040 2100 1037 3030
endmodule
